// Logisim project TallerLogica-Combinatorios.circ as structural Verilog: 13 circuits, main circuit verificador
module sumador_simple (
  input  a,
  input  b,
  output S,
  output Cout
);

  xor xor_1 (S, a, b);
  and and_1 (Cout, a, b);
endmodule

module sumador_completo (
  input  Cin,
  input  A,
  input  B,
  output S,
  output Cout
);

  wire sumador_simple_1_cout, sumador_simple_2_cout, sumador_simple_2_s;

  sumador_simple sumador_simple_1 (.a(Cin), .b(sumador_simple_2_s), .S(S), .Cout(sumador_simple_1_cout));
  sumador_simple sumador_simple_2 (.a(A), .b(B), .S(sumador_simple_2_s), .Cout(sumador_simple_2_cout));
  or or_1 (Cout, sumador_simple_1_cout, sumador_simple_2_cout);
endmodule

module sumador_4 (
  input  Cin,
  input  [3:0] A,
  input  [3:0] B,
  output [3:0] S,
  output Cout
);

  wire sumador_completo_1_cout, sumador_completo_2_cout, sumador_completo_3_cout;

  sumador_completo sumador_completo_1 (.A(A[0]), .B(B[0]), .Cin(Cin), .S(S[0]), .Cout(sumador_completo_1_cout));
  sumador_completo sumador_completo_2 (
    .A(A[1]), .B(B[1]), .Cin(sumador_completo_1_cout), .S(S[1]), .Cout(sumador_completo_2_cout));
  sumador_completo sumador_completo_3 (
    .A(A[2]), .B(B[2]), .Cin(sumador_completo_2_cout), .S(S[2]), .Cout(sumador_completo_3_cout));
  sumador_completo sumador_completo_4 (.A(A[3]), .B(B[3]), .Cin(sumador_completo_3_cout), .S(S[3]), .Cout(Cout));
  Hex_Digit_Display hex_digit_display_1 (.value(S));  // open: dp
endmodule

module comparador_cero (
  input  [3:0] A,
  output Z
);

  nor nor_1 (Z, A[0], A[1], A[2], A[3]);
endmodule

module sumador_flags (
  input  Cin,
  input  [3:0] A,
  input  [3:0] B,
  output [3:0] S,
  output N,
  output Z,
  output V,
  output C
);

  wire and_1_out, and_2_out, not_1_out, not_2_out, not_3_out, not_4_out, or_2_out, sumador_4_1_cout;
  wire [3:0] and_bit_a_bit_4_1_s;

  sumador_4 sumador_4_1 (.Cin(Cin), .A(A), .S({N, S[2:0]}), .B(B), .Cout(sumador_4_1_cout));
  not not_1 (not_1_out, A[3]);
  not not_2 (not_2_out, B[3]);
  not not_3 (not_3_out, N);
  AND_bit_a_bit_4 and_bit_a_bit_4_1 (.A(A), .B(B), .S(and_bit_a_bit_4_1_s));
  and and_1 (and_1_out, not_1_out, not_2_out, N);
  and and_2 (and_2_out, not_3_out, A[3], B[3]);
  comparador_cero comparador_cero_1 (.A({N, S[2:0]}), .Z(Z));
  or or_1 (V, and_1_out, and_2_out);
  Hex_Digit_Display hex_digit_display_1 (.value({N, S[2:0]}));  // open: dp
  or or_2 (or_2_out, and_bit_a_bit_4_1_s[0], and_bit_a_bit_4_1_s[1], and_bit_a_bit_4_1_s[2], and_bit_a_bit_4_1_s[3]);
  Multiplexer #(.enable("false")) multiplexer_1 (.in0(sumador_4_1_cout), .in1(or_2_out), .out(C), .sel(not_4_out));
  not not_4 (not_4_out, 1'b1);

  assign S[3] = N;

  // Notes on the sheet:
  //   Para el flag "c" la duda es si detecta acarreo final o acarreo en cualquier momento de la suma. Ahora esta resuelto para detectar que ocurrio acarreo en cualquier momento. Si es solo final se cable con el Cout del sumador
  //   "0" implica el cableado directo del sumador, "1" la logica bit a bit
  //   con "0" verifica todos los resultados cuando se imlementa en la ALU
endmodule

module incrementador_4 (
  input  [3:0] A,
  output [3:0] S
);

  wire [3:3] not_1_out;

  not not_1 (not_1_out[3], 1'b1);
  sumador_4 sumador_4_1 (.Cin(not_1_out[3]), .A(A), .S(S), .B({{3{not_1_out[3]}}, 1'b1}));  // open: Cout
  Hex_Digit_Display hex_digit_display_1 (.value(S));  // open: dp
endmodule

module inversor_4 (
  input  [3:0] A,
  input  INV,
  output [3:0] S
);

  wire [3:0] complemento_a2_4_1_s;

  complemento_A2_4 complemento_a2_4_1 (.A(A), .S(complemento_a2_4_1_s));
  Multiplexer #(.width(4), .enable("false")) multiplexer_1 (.in0(A), .in1(complemento_a2_4_1_s), .out(S), .sel(INV));
  Hex_Digit_Display hex_digit_display_1 (.value(S));  // open: dp
endmodule

module ALU (
  input  [3:0] A,
  input  [1:0] OP,
  input  [3:0] B,
  output Z,
  output V,
  output C,
  output [3:0] S,
  output N
);

  wire comparador_cero_1_z, comparador_cero_2_z, not_1_out, not_2_out, sumador_flags_1_c, sumador_flags_1_n,
       sumador_flags_1_v, sumador_flags_1_z, sumador_flags_2_c, sumador_flags_2_n, sumador_flags_2_v,
       sumador_flags_2_z;
  wire [3:0] and_bit_a_bit_4_1_s, complemento_a2_4_1_s, or_bit_a_bit_4_1_s, sumador_flags_1_s,
       sumador_flags_2_s;

  not not_1 (not_1_out, 1'b1);
  sumador_flags sumador_flags_1 (
    .A(A), .B(complemento_a2_4_1_s), .Cin(not_1_out), .S(sumador_flags_1_s), .N(sumador_flags_1_n),
    .Z(sumador_flags_1_z), .V(sumador_flags_1_v), .C(sumador_flags_1_c));
  complemento_A2_4 complemento_a2_4_1 (.A(B), .S(complemento_a2_4_1_s));
  AND_bit_a_bit_4 and_bit_a_bit_4_1 (.A(A), .B(B), .S(and_bit_a_bit_4_1_s));
  OR_bit_a_bit_4 or_bit_a_bit_4_1 (.A(A), .B(B), .S(or_bit_a_bit_4_1_s));
  sumador_flags sumador_flags_2 (
    .A(A), .B(B), .Cin(not_1_out), .S(sumador_flags_2_s), .N(sumador_flags_2_n), .Z(sumador_flags_2_z),
    .V(sumador_flags_2_v), .C(sumador_flags_2_c));
  Multiplexer #(.select(2), .width(4), .enable("false")) multiplexer_1 (
    .in0(sumador_flags_2_s), .in1(sumador_flags_1_s), .in2(and_bit_a_bit_4_1_s), .in3(or_bit_a_bit_4_1_s),
    .out(S), .sel(OP));
  not not_2 (not_2_out, sumador_flags_1_c);
  comparador_cero comparador_cero_1 (.A(and_bit_a_bit_4_1_s), .Z(comparador_cero_1_z));
  comparador_cero comparador_cero_2 (.A(or_bit_a_bit_4_1_s), .Z(comparador_cero_2_z));
  Multiplexer #(.select(2), .enable("false")) multiplexer_2 (
    .in0(sumador_flags_2_v), .in1(sumador_flags_1_v), .in2(not_1_out), .in3(not_1_out), .out(V), .sel(OP));
  Multiplexer #(.select(2), .enable("false")) multiplexer_3 (
    .in0(sumador_flags_2_c), .in1(not_2_out), .in2(not_1_out), .in3(not_1_out), .out(C), .sel(OP));
  Multiplexer #(.select(2), .enable("false")) multiplexer_4 (
    .in0(sumador_flags_2_z), .in1(sumador_flags_1_z), .in2(comparador_cero_1_z), .in3(comparador_cero_2_z),
    .out(Z), .sel(OP));
  Hex_Digit_Display hex_digit_display_1 (.value(S));  // open: dp
  Multiplexer #(.select(2), .enable("false")) multiplexer_5 (
    .in0(sumador_flags_2_n), .in1(sumador_flags_1_n), .in2(and_bit_a_bit_4_1_s[3]),
    .in3(or_bit_a_bit_4_1_s[3]), .out(N), .sel(OP));
endmodule

module verificador (
  output [3:0] a,
  output [3:0] b,
  output [1:0] Op,
  output N,
  output Z,
  output V,
  output C,
  output [3:0] Res,
  output halt
);

  wire clock_1_out;

  Clock clock_1 (.out(clock_1_out));
  Counter #(.width(10), .max('h3ff)) counter_1 (
    .Q({Op, b, a}), .carry(halt), .clk(clock_1_out));  // open: load, D, count, clr
  ALU alu_1 (.A(a), .B(b), .OP(Op), .Z(Z), .V(V), .C(C), .S(Res), .N(N));
endmodule

module complemento_A2_4 (
  input  [3:0] A,
  output [3:0] S
);

  wire [3:0] not_1_out;

  not not_1 (not_1_out[0], A[0]);
  not not_2 (not_1_out[1], A[1]);
  not not_3 (not_1_out[2], A[2]);
  not not_4 (not_1_out[3], A[3]);
  incrementador_4 incrementador_4_1 (.A(not_1_out), .S(S));
endmodule

module AND_bit_a_bit_4 (
  input  [3:0] A,
  input  [3:0] B,
  output [3:0] S
);

  and and_1 (S[0], A[0], B[0]);
  and and_2 (S[1], A[1], B[1]);
  and and_3 (S[2], A[2], B[2]);
  and and_4 (S[3], A[3], B[3]);
endmodule

module OR_bit_a_bit_4 (
  input  [3:0] A,
  input  [3:0] B,
  output [3:0] S
);

  or or_1 (S[0], A[0], B[0]);
  or or_2 (S[1], A[1], B[1]);
  or or_3 (S[2], A[2], B[2]);
  or or_4 (S[3], A[3], B[3]);
endmodule

module ejercicio_overflow_i (
  input  [3:0] A,
  input  [3:0] B,
  input  [1:0] OP,
  output Z,
  output C,
  output N,
  output V,
  output [3:0] S
);

  wire not_1_out;

  not not_1 (not_1_out, 1'b1);
  ALU alu_1 (.A(A), .B(B), .OP(OP), .Z(Z), .C(C), .S(S), .N(N));  // open: V
  Hex_Digit_Display hex_digit_display_1 (.value(S));  // open: dp
  Multiplexer #(.select(2), .enable("false")) multiplexer_1 (
    .in0(S[3]), .in1(S[3]), .in2(not_1_out), .in3(not_1_out), .out(V), .sel(OP));

  // Notes on the sheet:
  //   Es necasario un bit mas en la pabra de saluida (resultado) para detectarlo. 
  //   Este ejercicio muestra como detactar el overflow usando la ALU con palabras unsugned.
  //   Este ejemplo aplica a todo los modos con  palabras de entrada A y B de 3 bit, usando el 4 como indicador de V
endmodule
